# Fritzing sketch Schematic (saved by Fritzing 0.9.10b)
breadboards: 1

parts:
  Raspberry_Pi_1 = Raspberry Pi 3 [part_number=RPI-3-V1.2]
  S1 = Pushbutton [package="[THT]"]
  S2 = Pushbutton [package="[THT]"]
  S3 = Pushbutton [package="[THT]"]
  S4 = Pushbutton [package="[THT]"]
  LED1 = smd LED [color="Red (633nm)" package="0805 [SMD]"]
  LED2 = smd LED [color="Green (570nm)" package="0805 [SMD]"]
  R1 = Resistor [tolerance=±5% resistance=220 package="0402 [SMD]"]
  R2 = Resistor [tolerance=±5% resistance=220 package="0402 [SMD]"]

nets:
  N1: Raspberry_Pi_1.GPIO2, S1.Pin_1, S1.Pin_2
  N2: Raspberry_Pi_1.GPIO3, S2.Pin_1, S2.Pin_2
  N3: Raspberry_Pi_1.GPIO4, S3.Pin_1, S3.Pin_2
  N4: Raspberry_Pi_1.GPIO17, S4.Pin_1, S4.Pin_2
  N5: Raspberry_Pi_1.GPIO23, LED2.anode
  N6: Raspberry_Pi_1.GPIO15, LED1.anode
  N7: Raspberry_Pi_1.GND, S1.Pin_3, S1.Pin_4, S2.Pin_3, S2.Pin_4, S3.Pin_3, S3.Pin_4, S4.Pin_3, S4.Pin_4, R1.Pin_0, R2.Pin_0
  N8: LED1.cathode, R2.Pin_1
  N9: LED2.cathode, R1.Pin_1
